// Logisim project TestProject.circ as structural Verilog: 6 circuits, main circuit main
module main (
  input  DataInput1,
  input  DataInput2,
  input  DataInput3,
  input  DataInput4,
  input  in_5,
  output out_6,
  output out_7,
  output out_8
);

  wire add, add_or_sub_instr, ADD_TICK_1, ADD_TICK_2, ADD_TICK_3, ADD_TICK_4, alu_1_aout2, alu_1_aout3,
       alu_1_aout4, alu_2_aout3, alu_2_aout4, ALU_output_0, ALU_output_1, ALU_output_2, ALU_output_3,
       and_1_out, and_2_out, and_3_out, and_4_out, and_5_out, and_6_out, and_7_out, and_8_out, and_9_out,
       and_10_out, and_11_out, and_12_out, and_13_out, and_14_out, and_15_out, and_16_out, and_17_out,
       and_18_out, and_19_out, and_20_out, and_21_out, and_22_out, and_23_out, and_24_out, and_25_out,
       and_26_out, and_27_out, and_28_out, and_29_out, and_30_out, and_31_out, and_32_out, and_33_out,
       and_34_out, and_35_out, and_36_out, and_37_out, and_38_out, and_39_out, and_40_out, and_41_out,
       and_42_out, and_43_out, and_44_out, and_45_out, and_46_out, and_47_out, and_48_out, and_49_out,
       and_50_out, and_51_out, and_52_out, and_53_out, and_54_out, and_55_out, and_56_out, and_57_out,
       and_58_out, and_59_out, and_60_out, and_61_out, and_62_out, and_63_out, and_64_out, and_65_out,
       and_66_out, and_67_out, and_68_out, and_69_out, and_70_out, and_71_out, and_72_out, and_73_out,
       and_74_out, and_75_out, and_76_out, and_77_out, and_78_out, and_79_out, and_80_out, and_81_out,
       and_82_out, and_83_out, and_110_out, and_111_out, and_112_out, and_113_out, and_114_out, and_115_out,
       and_116_out, and_117_out, and_118_out, and_119_out, and_120_out, and_121_out, and_122_out,
       and_123_out, and_124_out, and_125_out, and_126_out, and_127_out, and_128_out, and_129_out,
       and_130_out, and_131_out, and_132_out, and_133_out, and_134_out, and_135_out, and_136_out,
       and_137_out, and_138_out, and_139_out, and_140_out, and_141_out, and_142_out, and_143_out,
       and_144_out, and_145_out, and_146_out, and_147_out, and_148_out, and_149_out, and_150_out,
       and_151_out, and_152_out, and_153_out, and_154_out, and_155_out, and_156_out, and_157_out,
       and_158_out, and_159_out, and_160_out, clk, clock_1_out, d_ff_1_q, d_ff_2_q, d_ff_3_q, d_ff_4_q,
       d_ff_5_q, d_ff_6_q, d_ff_7_q, d_ff_8_q, d_ff_9_q, d_ff_10_q, d_ff_11_q, d_ff_12_q, d_ff_13_q,
       d_ff_14_q, d_ff_15_q, d_ff_16_q, d_ff_17_q, d_ff_18_q, d_ff_19_q, d_ff_20_q, d_ff_21_q, d_ff_22_q,
       d_ff_23_q, d_ff_24_q, d_ff_25_q, d_ff_26_q, d_ff_27_q, d_ff_28_q, d_ff_29_q, d_ff_30_q, d_ff_31_q,
       d_ff_32_q, d_ff_33_q, d_ff_34_q, d_ff_35_q, d_ff_36_q, d_ff_37_q, d_ff_38_q, d_ff_39_q, d_ff_40_q,
       d_ff_41_q, d_ff_44_q, d_ff_44_qn, d_ff_45_q, d_ff_46_q, d_ff_47_q, d_ff_48_q, d_ff_49_q, d_ff_50_q,
       d_ff_51_q, d_ff_52_q, d_ff_53_q, d_ff_54_q, d_ff_55_q, d_ff_56_q, d_ff_57_q, d_ff_58_q, d_ff_59_q,
       d_ff_60_q, d_ff_61_q, d_ff_62_q, d_ff_63_q, d_ff_64_q, d_ff_65_q, d_ff_66_q, d_ff_67_q, data_address,
       data_input_0, data_input_1, data_input_2, data_input_3, data_output_0, data_output_1, data_output_2,
       data_output_3, datamode, fetch_out, halt, Halt_out, load, LOAD_TICK_1, LOAD_TICK_2, LOAD_TICK_3,
       LOAD_TICK_4, not_1_out, not_2_out, not_3_out, not_4_out, not_5_out, not_6_out, not_7_out, not_8_out,
       not_9_out, not_10_out, not_11_out, not_12_out, not_13_out, not_14_out, not_15_out, not_16_out,
       not_17_out, not_18_out, not_19_out, not_21_out, not_22_out, not_23_out, not_24_out, not_25_out,
       not_26_out, not_27_out, not_28_out, not_29_out, not_30_out, not_31_out, not_32_out, not_33_out,
       not_34_out, not_35_out, not_36_out, not_37_out, not_40_out, not_41_out, not_42_out, not_43_out,
       not_44_out, not_45_out, not_46_out, not_47_out, not_48_out, or_1_out, or_2_out, or_3_out, or_4_out,
       or_5_out, or_6_out, or_7_out, or_8_out, or_9_out, or_10_out, or_11_out, or_12_out, or_13_out,
       or_17_out, or_18_out, or_20_out, or_21_out, or_24_out, register_address, register_address_LOAD_SAVE,
       register_input_0_LOAD_SAVE, register_input_1_LOAD_SAVE, register_input_2_LOAD_SAVE,
       register_input_3_LOAD_SAVE, register_mode, register_mode_LOAD_SAVE, register_output_0,
       register_output_1, register_output_2, register_output_3, save, SAVE_TICK_1, SAVE_TICK_2, SAVE_TICK_3,
       SAVE_TICK_4, sub, SUB_TICK_1, SUB_TICK_2, SUB_TICK_3, SUB_TICK_4;
  wire [3:0] and_164_out, and_168_out;

  ALU alu_1 (
    .L2(d_ff_1_q), .L3(d_ff_2_q), .L4(d_ff_3_q), .R4(or_1_out), .clk(clk), .AOUT2(alu_1_aout2),
    .AOUT3(alu_1_aout3), .AOUT4(alu_1_aout4));  // open: L1, R1, R2, R3, cmd, Zero, Negative, Overflow, SignedOverflow, AOUT1
  or or_1 (or_1_out, ADD_TICK_3, LOAD_TICK_3, SAVE_TICK_3, SUB_TICK_3);
  D_Flip_Flop #(.trigger("falling")) d_ff_1 (.D(alu_1_aout2), .clk(clk), .Q(d_ff_1_q));  // open: Qn, preset, reset
  D_Flip_Flop #(.trigger("falling")) d_ff_2 (.D(alu_1_aout3), .clk(clk), .Q(d_ff_2_q));  // open: Qn, preset, reset
  D_Flip_Flop #(.trigger("falling")) d_ff_3 (.D(alu_1_aout4), .clk(clk), .Q(d_ff_3_q));  // open: Qn, preset, reset
  not not_1 (not_1_out, d_ff_3_q);
  not not_2 (not_2_out, d_ff_2_q);
  not not_3 (not_3_out, d_ff_2_q);
  not not_4 (not_4_out, d_ff_3_q);
  not not_5 (not_5_out, d_ff_1_q);
  not not_6 (not_6_out, d_ff_1_q);
  not not_7 (not_7_out, d_ff_3_q);
  not not_8 (not_8_out, d_ff_1_q);
  not not_9 (not_9_out, d_ff_2_q);
  not not_10 (not_10_out, d_ff_1_q);
  not not_11 (not_11_out, d_ff_2_q);
  not not_12 (not_12_out, d_ff_3_q);
  and and_1 (and_1_out, d_ff_1_q, d_ff_2_q, clk, d_ff_3_q);
  and and_2 (and_2_out, and_1_out, not_14_out);
  and and_3 (and_3_out, d_ff_1_q, d_ff_2_q, clk, not_1_out);
  and and_4 (and_4_out, and_3_out, not_14_out);
  and and_5 (and_5_out, d_ff_1_q, not_2_out, clk, d_ff_3_q);
  and and_6 (and_6_out, and_5_out, not_14_out);
  and and_7 (and_7_out, d_ff_1_q, not_3_out, clk, not_4_out);
  and and_8 (and_8_out, and_7_out, not_14_out);
  and and_9 (and_9_out, not_5_out, d_ff_2_q, clk, d_ff_3_q);
  and and_10 (and_10_out, and_9_out, not_14_out);
  and and_11 (and_11_out, not_6_out, d_ff_2_q, clk, not_7_out);
  and and_12 (and_12_out, and_11_out, not_14_out);
  and and_13 (and_13_out, not_8_out, not_9_out, clk, d_ff_3_q);
  and and_14 (and_14_out, and_13_out, not_14_out);
  and and_15 (and_15_out, not_10_out, not_11_out, clk, not_12_out);
  and and_16 (and_16_out, and_15_out, not_14_out);
  not not_13 (not_13_out, in_5);
  not not_14 (not_14_out, not_13_out);
  and and_17 (and_17_out, and_1_out, not_14_out, d_ff_12_q);
  D_Flip_Flop #(.trigger("high")) d_ff_4 (.D(and_17_out), .clk(and_2_out), .Q(d_ff_4_q));  // open: Qn, preset, reset
  and and_18 (and_18_out, and_3_out, not_14_out, d_ff_12_q);
  D_Flip_Flop #(.trigger("high")) d_ff_5 (.D(and_18_out), .clk(and_4_out), .Q(d_ff_5_q));  // open: Qn, preset, reset
  and and_19 (and_19_out, and_5_out, not_14_out, d_ff_12_q);
  D_Flip_Flop #(.trigger("high")) d_ff_6 (.D(and_19_out), .clk(and_6_out), .Q(d_ff_6_q));  // open: Qn, preset, reset
  and and_20 (and_20_out, and_7_out, not_14_out, d_ff_12_q);
  D_Flip_Flop #(.trigger("high")) d_ff_7 (.D(and_20_out), .clk(and_8_out), .Q(d_ff_7_q));  // open: Qn, preset, reset
  and and_21 (and_21_out, and_9_out, not_14_out, d_ff_12_q);
  D_Flip_Flop #(.trigger("high")) d_ff_8 (.D(and_21_out), .clk(and_10_out), .Q(d_ff_8_q));  // open: Qn, preset, reset
  and and_22 (and_22_out, and_11_out, not_14_out, d_ff_12_q);
  D_Flip_Flop #(.trigger("high")) d_ff_9 (.D(and_22_out), .clk(and_12_out), .Q(d_ff_9_q));  // open: Qn, preset, reset
  and and_23 (and_23_out, and_13_out, not_14_out, d_ff_12_q);
  D_Flip_Flop #(.trigger("high")) d_ff_10 (.D(and_23_out), .clk(and_14_out), .Q(d_ff_10_q));  // open: Qn, preset, reset
  and and_24 (and_24_out, and_15_out, not_14_out, d_ff_12_q);
  D_Flip_Flop #(.trigger("high")) d_ff_11 (.D(and_24_out), .clk(and_16_out), .Q(d_ff_11_q));  // open: Qn, preset, reset
  D_Flip_Flop #(.trigger("falling")) d_ff_12 (.D(DataInput1), .clk(clk), .Q(d_ff_12_q));  // open: Qn, preset, reset
  or or_2 (or_2_out, and_25_out, and_26_out, and_27_out, and_28_out, and_29_out, and_30_out, and_31_out, and_32_out);
  and and_25 (and_25_out, d_ff_4_q, and_1_out, not_13_out);
  and and_26 (and_26_out, d_ff_5_q, and_3_out, not_13_out);
  and and_27 (and_27_out, d_ff_6_q, and_5_out, not_13_out);
  and and_28 (and_28_out, d_ff_7_q, and_7_out, not_13_out);
  and and_29 (and_29_out, d_ff_8_q, and_9_out, not_13_out);
  and and_30 (and_30_out, d_ff_9_q, and_11_out, not_13_out);
  and and_31 (and_31_out, d_ff_10_q, and_13_out, not_13_out);
  and and_32 (and_32_out, d_ff_11_q, and_15_out, not_13_out);
  D_Flip_Flop #(.trigger("falling")) d_ff_13 (.D(DataInput2), .clk(clk), .Q(d_ff_13_q));  // open: Qn, preset, reset
  and and_33 (and_33_out, and_1_out, not_14_out, d_ff_13_q);
  D_Flip_Flop #(.trigger("high")) d_ff_14 (.D(and_33_out), .clk(and_2_out), .Q(d_ff_14_q));  // open: Qn, preset, reset
  and and_34 (and_34_out, and_3_out, not_14_out, d_ff_13_q);
  D_Flip_Flop #(.trigger("high")) d_ff_15 (.D(and_34_out), .clk(and_4_out), .Q(d_ff_15_q));  // open: Qn, preset, reset
  and and_35 (and_35_out, and_5_out, not_14_out, d_ff_13_q);
  D_Flip_Flop #(.trigger("high")) d_ff_16 (.D(and_35_out), .clk(and_6_out), .Q(d_ff_16_q));  // open: Qn, preset, reset
  and and_36 (and_36_out, and_7_out, not_14_out, d_ff_13_q);
  D_Flip_Flop #(.trigger("high")) d_ff_17 (.D(and_36_out), .clk(and_8_out), .Q(d_ff_17_q));  // open: Qn, preset, reset
  and and_37 (and_37_out, and_9_out, not_14_out, d_ff_13_q);
  D_Flip_Flop #(.trigger("high")) d_ff_18 (.D(and_37_out), .clk(and_10_out), .Q(d_ff_18_q));  // open: Qn, preset, reset
  and and_38 (and_38_out, and_11_out, not_14_out, d_ff_13_q);
  D_Flip_Flop #(.trigger("high")) d_ff_19 (.D(and_38_out), .clk(and_12_out), .Q(d_ff_19_q));  // open: Qn, preset, reset
  and and_39 (and_39_out, and_13_out, not_14_out, d_ff_13_q);
  D_Flip_Flop #(.trigger("high")) d_ff_20 (.D(and_39_out), .clk(and_14_out), .Q(d_ff_20_q));  // open: Qn, preset, reset
  and and_40 (and_40_out, and_15_out, not_14_out, d_ff_13_q);
  D_Flip_Flop #(.trigger("high")) d_ff_21 (.D(and_40_out), .clk(and_16_out), .Q(d_ff_21_q));  // open: Qn, preset, reset
  D_Flip_Flop #(.trigger("falling")) d_ff_22 (.D(DataInput3), .clk(clk), .Q(d_ff_22_q));  // open: Qn, preset, reset
  or or_3 (or_3_out, and_41_out, and_42_out, and_43_out, and_44_out, and_45_out, and_46_out, and_47_out, and_48_out);
  and and_41 (and_41_out, d_ff_14_q, and_1_out, not_13_out);
  and and_42 (and_42_out, d_ff_15_q, and_3_out, not_13_out);
  and and_43 (and_43_out, d_ff_16_q, and_5_out, not_13_out);
  and and_44 (and_44_out, d_ff_17_q, and_7_out, not_13_out);
  and and_45 (and_45_out, d_ff_18_q, and_9_out, not_13_out);
  and and_46 (and_46_out, d_ff_19_q, and_11_out, not_13_out);
  and and_47 (and_47_out, d_ff_20_q, and_13_out, not_13_out);
  and and_48 (and_48_out, d_ff_21_q, and_15_out, not_13_out);
  D_Flip_Flop #(.trigger("falling")) d_ff_23 (.D(DataInput4), .clk(clk), .Q(d_ff_23_q));  // open: Qn, preset, reset
  and and_49 (and_49_out, and_1_out, not_14_out, d_ff_22_q);
  D_Flip_Flop #(.trigger("high")) d_ff_24 (.D(and_49_out), .clk(and_2_out), .Q(d_ff_24_q));  // open: Qn, preset, reset
  and and_50 (and_50_out, and_3_out, not_14_out, d_ff_22_q);
  D_Flip_Flop #(.trigger("high")) d_ff_25 (.D(and_50_out), .clk(and_4_out), .Q(d_ff_25_q));  // open: Qn, preset, reset
  and and_51 (and_51_out, and_5_out, not_14_out, d_ff_22_q);
  D_Flip_Flop #(.trigger("high")) d_ff_26 (.D(and_51_out), .clk(and_6_out), .Q(d_ff_26_q));  // open: Qn, preset, reset
  and and_52 (and_52_out, and_7_out, not_14_out, d_ff_22_q);
  D_Flip_Flop #(.trigger("high")) d_ff_27 (.D(and_52_out), .clk(and_8_out), .Q(d_ff_27_q));  // open: Qn, preset, reset
  and and_53 (and_53_out, and_9_out, not_14_out, d_ff_22_q);
  D_Flip_Flop #(.trigger("high")) d_ff_28 (.D(and_53_out), .clk(and_10_out), .Q(d_ff_28_q));  // open: Qn, preset, reset
  and and_54 (and_54_out, and_11_out, not_14_out, d_ff_22_q);
  D_Flip_Flop #(.trigger("high")) d_ff_29 (.D(and_54_out), .clk(and_12_out), .Q(d_ff_29_q));  // open: Qn, preset, reset
  and and_55 (and_55_out, and_13_out, not_14_out, d_ff_22_q);
  D_Flip_Flop #(.trigger("high")) d_ff_30 (.D(and_55_out), .clk(and_14_out), .Q(d_ff_30_q));  // open: Qn, preset, reset
  and and_56 (and_56_out, and_15_out, not_14_out, d_ff_22_q);
  D_Flip_Flop #(.trigger("high")) d_ff_31 (.D(and_56_out), .clk(and_16_out), .Q(d_ff_31_q));  // open: Qn, preset, reset
  or or_4 (or_4_out, and_57_out, and_58_out, and_59_out, and_60_out, and_61_out, and_62_out, and_63_out, and_64_out);
  and and_57 (and_57_out, and_1_out, d_ff_24_q, not_13_out);
  and and_58 (and_58_out, d_ff_25_q, and_3_out, not_13_out);
  and and_59 (and_59_out, d_ff_26_q, and_5_out, not_13_out);
  and and_60 (and_60_out, d_ff_27_q, and_7_out, not_13_out);
  and and_61 (and_61_out, d_ff_28_q, and_9_out, not_13_out);
  and and_62 (and_62_out, d_ff_29_q, and_11_out, not_13_out);
  and and_63 (and_63_out, d_ff_30_q, and_13_out, not_13_out);
  and and_64 (and_64_out, d_ff_31_q, and_15_out, not_13_out);
  and and_65 (and_65_out, and_1_out, not_14_out, d_ff_23_q);
  D_Flip_Flop #(.trigger("high")) d_ff_32 (.D(and_65_out), .clk(and_2_out), .Q(d_ff_32_q));  // open: Qn, preset, reset
  and and_66 (and_66_out, and_3_out, not_14_out, d_ff_23_q);
  D_Flip_Flop #(.trigger("high")) d_ff_33 (.D(and_66_out), .clk(and_4_out), .Q(d_ff_33_q));  // open: Qn, preset, reset
  and and_67 (and_67_out, and_5_out, not_14_out, d_ff_23_q);
  D_Flip_Flop #(.trigger("high")) d_ff_34 (.D(and_67_out), .clk(and_6_out), .Q(d_ff_34_q));  // open: Qn, preset, reset
  and and_68 (and_68_out, and_7_out, not_14_out, d_ff_23_q);
  D_Flip_Flop #(.trigger("high")) d_ff_35 (.D(and_68_out), .clk(and_8_out), .Q(d_ff_35_q));  // open: Qn, preset, reset
  and and_69 (and_69_out, and_9_out, not_14_out, d_ff_23_q);
  D_Flip_Flop #(.trigger("high")) d_ff_36 (.D(and_69_out), .clk(and_10_out), .Q(d_ff_36_q));  // open: Qn, preset, reset
  and and_70 (and_70_out, and_11_out, not_14_out, d_ff_23_q);
  D_Flip_Flop #(.trigger("high")) d_ff_37 (.D(and_70_out), .clk(and_12_out), .Q(d_ff_37_q));  // open: Qn, preset, reset
  and and_71 (and_71_out, and_13_out, not_14_out, d_ff_23_q);
  D_Flip_Flop #(.trigger("high")) d_ff_38 (.D(and_71_out), .clk(and_14_out), .Q(d_ff_38_q));  // open: Qn, preset, reset
  and and_72 (and_72_out, and_15_out, not_14_out, d_ff_23_q);
  D_Flip_Flop #(.trigger("high")) d_ff_39 (.D(and_72_out), .clk(and_16_out), .Q(d_ff_39_q));  // open: Qn, preset, reset
  or or_5 (or_5_out, and_73_out, and_74_out, and_75_out, and_76_out, and_77_out, and_78_out, and_79_out, and_80_out);
  and and_73 (and_73_out, d_ff_32_q, and_1_out, not_13_out);
  and and_74 (and_74_out, d_ff_33_q, and_3_out, not_13_out);
  and and_75 (and_75_out, d_ff_34_q, and_5_out, not_13_out);
  and and_76 (and_76_out, d_ff_35_q, and_7_out, not_13_out);
  and and_77 (and_77_out, d_ff_36_q, and_9_out, not_13_out);
  and and_78 (and_78_out, d_ff_37_q, and_11_out, not_13_out);
  and and_79 (and_79_out, d_ff_38_q, and_13_out, not_13_out);
  and and_80 (and_80_out, d_ff_39_q, and_15_out, not_13_out);
  D_Flip_Flop #(.trigger("falling")) d_ff_40 (.D(or_2_out), .clk(clk), .Q(d_ff_40_q));  // open: Qn, preset, reset
  D_Flip_Flop #(.trigger("falling")) d_ff_41 (.D(or_3_out), .clk(clk), .Q(d_ff_41_q));  // open: Qn, preset, reset
  D_Flip_Flop #(.trigger("falling")) d_ff_42 (
    .D(or_4_out), .clk(clk), .Q(register_address_LOAD_SAVE));  // open: Qn, preset, reset
  D_Flip_Flop #(.trigger("falling")) d_ff_43 (.D(or_5_out), .clk(clk), .Q(data_address));  // open: Qn, preset, reset
  and and_81 (and_81_out, register_address_LOAD_SAVE, data_address);
  not not_15 (not_15_out, d_ff_40_q);
  not not_16 (not_16_out, d_ff_41_q);
  not not_17 (not_17_out, d_ff_40_q);
  not not_18 (not_18_out, d_ff_41_q);
  not not_19 (not_19_out, and_81_out);
  D_Flip_Flop #(.trigger("falling")) d_ff_44 (
    .D(d_ff_44_qn), .clk(clk), .Q(d_ff_44_q), .Qn(d_ff_44_qn));  // open: preset, reset
  and u_Load (load, not_15_out, not_16_out);
  and u_Save (save, not_17_out, d_ff_41_q);
  and u_Add (add, d_ff_40_q, not_18_out);
  and u_Sub (sub, d_ff_40_q, not_19_out, d_ff_41_q);
  and u_Halt (Halt_out, d_ff_41_q, and_81_out, d_ff_40_q);
  not not_20 (halt, Halt_out);
  or or_6 (or_6_out, and_82_out, and_83_out);
  and and_82 (and_82_out, d_ff_45_q, not_21_out);
  and and_83 (and_83_out, d_ff_44_q, d_ff_44_q);
  not not_21 (not_21_out, d_ff_44_q);
  D_Flip_Flop #(.trigger("falling")) d_ff_45 (.D(or_6_out), .clk(clk), .Q(d_ff_45_q));  // open: Qn, preset, reset
  and fetch (fetch_out, d_ff_45_q, load);
  and and_84 (add_or_sub_instr, d_ff_40_q, d_ff_41_q);
  D_Flip_Flop #(.trigger("falling")) d_ff_46 (.D(alu_2_aout3), .clk(clk), .Q(d_ff_46_q));  // open: Qn, preset, reset
  D_Flip_Flop #(.trigger("falling")) d_ff_47 (.D(alu_2_aout4), .clk(clk), .Q(d_ff_47_q));  // open: Qn, preset, reset
  not not_22 (not_22_out, d_ff_46_q);
  not not_23 (not_23_out, d_ff_47_q);
  not not_24 (not_24_out, d_ff_46_q);
  not not_25 (not_25_out, d_ff_47_q);
  not not_26 (not_26_out, d_ff_46_q);
  not not_27 (not_27_out, d_ff_47_q);
  not not_28 (not_28_out, d_ff_46_q);
  not not_29 (not_29_out, d_ff_47_q);
  not not_30 (not_30_out, d_ff_46_q);
  not not_31 (not_31_out, d_ff_47_q);
  not not_32 (not_32_out, d_ff_46_q);
  not not_33 (not_33_out, d_ff_47_q);
  not not_34 (not_34_out, d_ff_46_q);
  not not_35 (not_35_out, d_ff_47_q);
  not not_36 (not_36_out, d_ff_46_q);
  not not_37 (not_37_out, d_ff_47_q);
  ALU alu_2 (
    .L4(or_7_out), .R3(d_ff_46_q), .R4(d_ff_47_q), .clk(clk), .AOUT3(alu_2_aout3), .AOUT4(alu_2_aout4));  // open: L1, L2, L3, R1, R2, cmd, Zero, Negative, Overflow, SignedOverflow, AOUT1, AOUT2
  or or_7 (or_7_out, LOAD_TICK_4, LOAD_TICK_3, ADD_TICK_1, ADD_TICK_2, ADD_TICK_3, ADD_TICK_4, SAVE_TICK_1, SAVE_TICK_2, LOAD_TICK_1, LOAD_TICK_2, SUB_TICK_1, SUB_TICK_2, SUB_TICK_3, SUB_TICK_4, SAVE_TICK_3, SAVE_TICK_4);
  and and_85 (LOAD_TICK_1, not_22_out, fetch_out, not_23_out);
  and and_86 (LOAD_TICK_2, not_24_out, fetch_out, d_ff_47_q);
  and and_87 (LOAD_TICK_3, d_ff_46_q, fetch_out, not_25_out);
  and and_88 (LOAD_TICK_4, d_ff_46_q, fetch_out, d_ff_47_q);
  and and_89 (SAVE_TICK_1, not_26_out, save, not_27_out);
  and and_90 (SAVE_TICK_2, not_28_out, save, d_ff_47_q);
  and and_91 (SAVE_TICK_3, d_ff_46_q, save, not_29_out);
  and and_92 (SAVE_TICK_4, d_ff_46_q, save, d_ff_47_q);
  and and_93 (ADD_TICK_1, not_30_out, add, not_31_out);
  and and_94 (ADD_TICK_2, not_32_out, add, d_ff_47_q);
  and and_95 (ADD_TICK_3, d_ff_46_q, add, not_33_out);
  and and_96 (ADD_TICK_4, d_ff_46_q, add, d_ff_47_q);
  and and_97 (SUB_TICK_1, not_34_out, sub, not_35_out);
  and and_98 (SUB_TICK_2, not_36_out, sub, d_ff_47_q);
  and and_99 (SUB_TICK_3, d_ff_46_q, sub, not_37_out);
  and and_100 (SUB_TICK_4, d_ff_46_q, sub, d_ff_47_q);
  and and_101 (register_input_0_LOAD_SAVE, data_output_0, fetch_out);
  and and_102 (register_input_1_LOAD_SAVE, data_output_1, fetch_out);
  and and_103 (register_input_2_LOAD_SAVE, data_output_2, fetch_out);
  and and_104 (register_input_3_LOAD_SAVE, data_output_3, fetch_out);
  and and_105 (data_input_0, register_output_0, save);
  and and_106 (data_input_1, register_output_1, save);
  and and_107 (data_input_2, register_output_2, save);
  and and_108 (data_input_3, register_output_3, save);
  not not_38 (datamode, save);
  or or_8 (or_8_out, ADD_TICK_1, SUB_TICK_1);
  or or_9 (or_9_out, ADD_TICK_2, SUB_TICK_2);
  and and_109 (clk, halt, clock_1_out);
  Clock clock_1 (.out(clock_1_out));
  not not_39 (register_mode_LOAD_SAVE, fetch_out);
  or or_10 (or_10_out, ADD_TICK_3, SUB_TICK_3);
  or or_11 (or_11_out, ADD_TICK_4, SUB_TICK_4);
  or or_12 (or_12_out, or_10_out, or_11_out);
  and and_110 (and_110_out, register_address_LOAD_SAVE, or_8_out);
  and and_111 (and_111_out, or_9_out, data_address);
  and and_112 (and_112_out, register_address_LOAD_SAVE, or_12_out);
  not not_40 (not_40_out, or_11_out);
  or or_13 (or_13_out, and_110_out, and_111_out, and_112_out);
  or or_14 (register_address, and_113_out, and_114_out);
  and and_113 (and_113_out, register_address_LOAD_SAVE, or_24_out);
  and and_114 (and_114_out, not_41_out, or_13_out);
  not not_41 (not_41_out, or_24_out);
  not not_42 (not_42_out, register_address);
  and and_115 (and_115_out, clk, register_address);
  and and_116 (and_116_out, clk, not_42_out);
  or or_15 (register_mode, and_117_out, and_118_out);
  and and_117 (and_117_out, register_mode_LOAD_SAVE, or_24_out);
  and and_118 (and_118_out, not_43_out, not_40_out);
  not not_43 (not_43_out, or_24_out);
  and and_119 (and_119_out, and_115_out, not_44_out);
  and and_120 (and_120_out, and_116_out, not_44_out);
  not not_44 (not_44_out, register_mode);
  and and_121 (and_121_out, and_115_out, not_44_out, d_ff_50_q);
  D_Flip_Flop #(.trigger("high")) d_ff_48 (
    .D(and_121_out), .clk(and_119_out), .Q(d_ff_48_q));  // open: Qn, preset, reset
  and and_122 (and_122_out, and_116_out, not_44_out, d_ff_50_q);
  D_Flip_Flop #(.trigger("high")) d_ff_49 (
    .D(and_122_out), .clk(and_120_out), .Q(d_ff_49_q));  // open: Qn, preset, reset
  or or_16 (register_output_3, and_123_out, and_124_out);
  and and_123 (and_123_out, d_ff_48_q, and_115_out, register_mode);
  and and_124 (and_124_out, d_ff_49_q, and_116_out, register_mode);
  D_Flip_Flop #(.trigger("falling")) d_ff_50 (.D(or_17_out), .clk(clk), .Q(d_ff_50_q));  // open: Qn, preset, reset
  or or_17 (or_17_out, and_125_out, and_126_out);
  and and_125 (and_125_out, ALU_output_3, not_45_out);
  and and_126 (and_126_out, or_24_out, register_input_3_LOAD_SAVE);
  not not_45 (not_45_out, or_24_out);
  D_Flip_Flop #(.trigger("falling")) d_ff_51 (.D(or_18_out), .clk(clk), .Q(d_ff_51_q));  // open: Qn, preset, reset
  or or_18 (or_18_out, and_127_out, and_128_out);
  and and_127 (and_127_out, ALU_output_2, not_46_out);
  and and_128 (and_128_out, or_24_out, register_input_2_LOAD_SAVE);
  not not_46 (not_46_out, or_24_out);
  or or_19 (register_output_2, and_133_out, and_134_out);
  and and_129 (and_129_out, and_115_out, not_44_out, d_ff_51_q);
  and and_130 (and_130_out, and_116_out, not_44_out, d_ff_51_q);
  D_Flip_Flop #(.trigger("falling")) d_ff_52 (.D(or_20_out), .clk(clk), .Q(d_ff_52_q));  // open: Qn, preset, reset
  or or_20 (or_20_out, and_131_out, and_132_out);
  and and_131 (and_131_out, ALU_output_1, not_47_out);
  and and_132 (and_132_out, or_24_out, register_input_1_LOAD_SAVE);
  not not_47 (not_47_out, or_24_out);
  and and_133 (and_133_out, d_ff_53_q, and_115_out, register_mode);
  D_Flip_Flop #(.trigger("high")) d_ff_53 (
    .D(and_129_out), .clk(and_119_out), .Q(d_ff_53_q));  // open: Qn, preset, reset
  and and_134 (and_134_out, d_ff_54_q, and_116_out, register_mode);
  D_Flip_Flop #(.trigger("high")) d_ff_54 (
    .D(and_130_out), .clk(and_120_out), .Q(d_ff_54_q));  // open: Qn, preset, reset
  D_Flip_Flop #(.trigger("falling")) d_ff_55 (.D(or_21_out), .clk(clk), .Q(d_ff_55_q));  // open: Qn, preset, reset
  or or_21 (or_21_out, and_135_out, and_136_out);
  and and_135 (and_135_out, ALU_output_0, not_48_out);
  and and_136 (and_136_out, or_24_out, register_input_0_LOAD_SAVE);
  not not_48 (not_48_out, or_24_out);
  or or_22 (register_output_1, and_139_out, and_140_out);
  or or_23 (register_output_0, and_159_out, and_160_out);
  and and_137 (and_137_out, and_115_out, not_44_out, d_ff_52_q);
  D_Flip_Flop #(.trigger("high")) d_ff_56 (
    .D(and_137_out), .clk(and_119_out), .Q(d_ff_56_q));  // open: Qn, preset, reset
  and and_138 (and_138_out, and_116_out, not_44_out, d_ff_52_q);
  D_Flip_Flop #(.trigger("high")) d_ff_57 (
    .D(and_138_out), .clk(and_120_out), .Q(d_ff_57_q));  // open: Qn, preset, reset
  or or_24 (or_24_out, load, save);
  and and_139 (and_139_out, d_ff_56_q, and_115_out, register_mode);
  and and_140 (and_140_out, d_ff_57_q, and_116_out, register_mode);
  and and_141 (and_141_out, and_115_out, not_44_out, d_ff_55_q);
  D_Flip_Flop #(.trigger("high")) d_ff_58 (
    .D(and_141_out), .clk(and_119_out), .Q(d_ff_58_q));  // open: Qn, preset, reset
  and and_142 (and_142_out, and_116_out, not_44_out, d_ff_55_q);
  D_Flip_Flop #(.trigger("high")) d_ff_59 (
    .D(and_142_out), .clk(and_120_out), .Q(d_ff_59_q));  // open: Qn, preset, reset
  D_Flip_Flop #(.trigger("high")) d_ff_60 (
    .D(and_143_out), .clk(and_144_out), .Q(d_ff_60_q));  // open: Qn, preset, reset
  and and_143 (and_143_out, register_output_3, or_8_out);
  and and_144 (and_144_out, or_8_out, clk);
  D_Flip_Flop #(.trigger("high")) d_ff_61 (
    .D(and_145_out), .clk(and_146_out), .Q(d_ff_61_q));  // open: Qn, preset, reset
  and and_145 (and_145_out, register_output_2, or_8_out);
  and and_146 (and_146_out, or_8_out, clk);
  D_Flip_Flop #(.trigger("high")) d_ff_62 (
    .D(and_147_out), .clk(and_148_out), .Q(d_ff_62_q));  // open: Qn, preset, reset
  and and_147 (and_147_out, register_output_1, or_8_out);
  and and_148 (and_148_out, or_8_out, clk);
  D_Flip_Flop #(.trigger("high")) d_ff_63 (
    .D(and_149_out), .clk(and_150_out), .Q(d_ff_63_q));  // open: Qn, preset, reset
  and and_149 (and_149_out, register_output_0, or_8_out);
  and and_150 (and_150_out, or_8_out, clk);
  D_Flip_Flop #(.trigger("high")) d_ff_64 (
    .D(and_151_out), .clk(and_152_out), .Q(d_ff_64_q));  // open: Qn, preset, reset
  and and_151 (and_151_out, register_output_3, or_9_out);
  and and_152 (and_152_out, or_9_out, clk);
  D_Flip_Flop #(.trigger("high")) d_ff_65 (
    .D(and_153_out), .clk(and_154_out), .Q(d_ff_65_q));  // open: Qn, preset, reset
  and and_153 (and_153_out, register_output_2, or_9_out);
  and and_154 (and_154_out, or_9_out, clk);
  D_Flip_Flop #(.trigger("high")) d_ff_66 (
    .D(and_155_out), .clk(and_156_out), .Q(d_ff_66_q));  // open: Qn, preset, reset
  and and_155 (and_155_out, register_output_1, or_9_out);
  and and_156 (and_156_out, or_9_out, clk);
  D_Flip_Flop #(.trigger("high")) d_ff_67 (
    .D(and_157_out), .clk(and_158_out), .Q(d_ff_67_q));  // open: Qn, preset, reset
  and and_157 (and_157_out, register_output_0, or_9_out);
  and and_158 (and_158_out, or_9_out, clk);
  and and_159 (and_159_out, d_ff_58_q, and_115_out, register_mode);
  and and_160 (and_160_out, d_ff_59_q, and_116_out, register_mode);
  and and_161 (and_164_out[3], d_ff_60_q, or_10_out);
  and and_162 (and_164_out[2], d_ff_61_q, or_10_out);
  and and_163 (and_164_out[1], d_ff_62_q, or_10_out);
  and and_164 (and_164_out[0], d_ff_63_q, or_10_out);
  and and_165 (and_168_out[3], d_ff_64_q, or_10_out);
  and and_166 (and_168_out[2], d_ff_65_q, or_10_out);
  and and_167 (and_168_out[1], d_ff_66_q, or_10_out);
  and and_168 (and_168_out[0], d_ff_67_q, or_10_out);
  ALU2 alu2_1 (
    .A(and_164_out), .B(and_168_out), .CLK(clk), .ADD_OR_SUB(add_or_sub_instr),
    .ALU_Output({ALU_output_3, ALU_output_2, ALU_output_1, ALU_output_0}), .Status({out_8, out_7, out_6}));
  Project_Data_RAM project_data_ram_1 (
    .CLK(clk), .Address_1Bit(data_address),
    .Data_Input({data_input_3, data_input_2, data_input_1, data_input_0}), .MODE(datamode),
    .Data_Output({data_output_3, data_output_2, data_output_1, data_output_0}));

  // Notes on the sheet:
  //   4 pins always +1
  //   PC
  //   Top pin always 0 for cmd
  //   PC address
  //   Mode input pin
  //   INverted: by default 1 to Read from I-RAM
  //   Instruction RAM
  //   IR
  //   INVERTED SO THAT THE REGISTER BLOCK IS IN READ MODE BY DEFAULT
  //   REGISTER BLOCK
  //   MULTIPLEXOR
  //   R1
  //   R0
  //   Need to add this for add/sub, need to specify which register to store to
  //   MULTIPLEXOR 
  //   B
  //   A
  //   ALU
  //   Status
  //   DATA RAM
endmodule

module Project_Instruction_RAM (
  input  CLK,
  input  MODE,
  input  [2:0] Address,
  input  [3:0] Instruction_Input,
  output [3:0] Instruction_Output
);

  wire and_1_out, and_2_out, and_3_out, and_4_out, and_5_out, and_6_out, and_7_out, and_8_out, and_9_out,
       and_10_out, and_11_out, and_12_out, B0, B0_I0, B0_I1, B0_I2, B0_I3, B0_I4, B0_I5, B0_I6, B0_I7, B1,
       B1_I0, B1_I1, B1_I2, B1_I3, B1_I4, B1_I5, B1_I6, B1_I7, B2, B2_I0, B2_I1, B2_I2, B2_I3, B2_I4, B2_I5,
       B2_I6, B2_I7, B3, B3_I0, B3_I1, B3_I2, B3_I3, B3_I4, B3_I5, B3_I6, B3_I7, d_ff_4_q, decoder_1_out0,
       decoder_1_out1, decoder_1_out2, decoder_1_out3, decoder_1_out4, decoder_1_out5, decoder_1_out6,
       decoder_1_out7, multiplexer_1_out, multiplexer_2_out, multiplexer_3_out, multiplexer_4_out, not_1_out;
  wire [2:0] MUX_SELECT;

  D_Flip_Flop d_ff_1 (.D(Address[2]), .clk(CLK), .Q(MUX_SELECT[2]));  // open: Qn, preset, reset
  D_Flip_Flop d_ff_2 (.D(Address[1]), .clk(CLK), .Q(MUX_SELECT[1]));  // open: Qn, preset, reset
  Decoder #(.select(3)) decoder_1 (
    .out0(decoder_1_out0), .out1(decoder_1_out1), .out2(decoder_1_out2), .out3(decoder_1_out3),
    .out4(decoder_1_out4), .out5(decoder_1_out5), .out6(decoder_1_out6), .out7(decoder_1_out7),
    .sel(MUX_SELECT));  // open: en
  D_Flip_Flop d_ff_3 (.D(Address[0]), .clk(CLK), .Q(MUX_SELECT[0]));  // open: Qn, preset, reset
  Multiplexer #(.select(3)) multiplexer_1 (
    .in0(B3_I0), .in1(B3_I1), .in2(B3_I2), .in3(B3_I3), .in4(B3_I4), .in5(B3_I5), .in6(B3_I6), .in7(B3_I7),
    .out(multiplexer_1_out), .sel(MUX_SELECT));
  Multiplexer #(.select(3)) multiplexer_2 (
    .in0(B2_I0), .in1(B2_I1), .in2(B2_I2), .in3(B2_I3), .in4(B2_I4), .in5(B2_I5), .in6(B2_I6), .in7(B2_I7),
    .out(multiplexer_2_out), .sel(MUX_SELECT));
  and and_1 (and_1_out, decoder_1_out0, not_1_out, CLK);
  and and_2 (and_2_out, decoder_1_out1, not_1_out, CLK);
  not not_1 (not_1_out, d_ff_4_q);
  D_Flip_Flop d_ff_4 (.D(MODE), .clk(CLK), .Q(d_ff_4_q));  // open: Qn, preset, reset
  and and_3 (and_3_out, decoder_1_out2, not_1_out, CLK);
  and and_4 (and_4_out, decoder_1_out3, not_1_out, CLK);
  Multiplexer #(.select(3)) multiplexer_3 (
    .in0(B1_I0), .in1(B1_I1), .in2(B1_I2), .in3(B1_I3), .in4(B1_I4), .in5(B1_I5), .in6(B1_I6), .in7(B1_I7),
    .out(multiplexer_3_out), .sel(MUX_SELECT));
  Multiplexer #(.select(3)) multiplexer_4 (
    .in0(B0_I0), .in1(B0_I1), .in2(B0_I2), .in3(B0_I3), .in4(B0_I4), .in5(B0_I5), .in6(B0_I6), .in7(B0_I7),
    .out(multiplexer_4_out), .sel(MUX_SELECT));
  Project_MyReg project_myreg_1 (
    .B3_IN(B3), .B2_IN(B2), .B1_IN(B1), .B0_IN(B0), .MyClock(and_1_out), .B3_OUT(B3_I0), .B2_OUT(B2_I0),
    .B1_OUT(B1_I0), .B0_OUT(B0_I0));
  Project_MyReg project_myreg_2 (
    .B3_IN(B3), .B2_IN(B2), .B1_IN(B1), .B0_IN(B0), .MyClock(and_3_out), .B3_OUT(B3_I2), .B2_OUT(B2_I2),
    .B1_OUT(B1_I2), .B0_OUT(B0_I2));
  Project_MyReg project_myreg_3 (
    .B3_IN(B3), .B2_IN(B2), .B1_IN(B1), .B0_IN(B0), .MyClock(and_2_out), .B3_OUT(B3_I1), .B2_OUT(B2_I1),
    .B1_OUT(B1_I1), .B0_OUT(B0_I1));
  Project_MyReg project_myreg_4 (
    .B3_IN(B3), .B2_IN(B2), .B1_IN(B1), .B0_IN(B0), .MyClock(and_4_out), .B3_OUT(B3_I3), .B2_OUT(B2_I3),
    .B1_OUT(B1_I3), .B0_OUT(B0_I3));
  and and_5 (and_5_out, multiplexer_3_out, d_ff_4_q);
  and and_6 (and_6_out, multiplexer_4_out, d_ff_4_q);
  and and_7 (and_7_out, multiplexer_1_out, d_ff_4_q);
  and and_8 (and_8_out, multiplexer_2_out, d_ff_4_q);
  and and_9 (and_9_out, decoder_1_out4, not_1_out, CLK);
  and and_10 (and_10_out, decoder_1_out5, not_1_out, CLK);
  Project_MyReg project_myreg_5 (
    .B3_IN(and_7_out), .B2_IN(and_8_out), .B1_IN(and_5_out), .B0_IN(and_6_out), .MyClock(CLK),
    .B3_OUT(Instruction_Output[3]), .B2_OUT(Instruction_Output[2]), .B1_OUT(Instruction_Output[1]),
    .B0_OUT(Instruction_Output[0]));
  and and_11 (and_11_out, decoder_1_out6, not_1_out, CLK);
  and and_12 (and_12_out, decoder_1_out7, not_1_out, CLK);
  Project_MyReg project_myreg_6 (
    .B3_IN(B3), .B2_IN(B2), .B1_IN(B1), .B0_IN(B0), .MyClock(and_11_out), .B3_OUT(B3_I6), .B2_OUT(B2_I6),
    .B1_OUT(B1_I6), .B0_OUT(B0_I6));
  Project_MyReg project_myreg_7 (
    .B3_IN(B3), .B2_IN(B2), .B1_IN(B1), .B0_IN(B0), .MyClock(and_10_out), .B3_OUT(B3_I5), .B2_OUT(B2_I5),
    .B1_OUT(B1_I5), .B0_OUT(B0_I5));
  Project_MyReg project_myreg_8 (
    .B3_IN(B3), .B2_IN(B2), .B1_IN(B1), .B0_IN(B0), .MyClock(and_12_out), .B3_OUT(B3_I7), .B2_OUT(B2_I7),
    .B1_OUT(B1_I7), .B0_OUT(B0_I7));

  // Other names for the same wires on the sheet: S0 = MUX_SELECT[0]; S1 = MUX_SELECT[1]; S2 = MUX_SELECT[2]

  // Notes on the sheet:
  //   CHOOSE_B3
  //   CHOOSE_B2
  //   CHOOSE_B1
  //   CHOOSE_B0
endmodule

module Project_MyReg (
  input  B3_IN,
  input  B2_IN,
  input  B1_IN,
  input  B0_IN,
  input  MyClock,
  output B3_OUT,
  output B2_OUT,
  output B1_OUT,
  output B0_OUT
);

  D_Flip_Flop d_ff_1 (.D(B3_IN), .clk(MyClock), .Q(B3_OUT));  // open: Qn, preset, reset
  D_Flip_Flop d_ff_2 (.D(B2_IN), .clk(MyClock), .Q(B2_OUT));  // open: Qn, preset, reset
  D_Flip_Flop d_ff_3 (.D(B1_IN), .clk(MyClock), .Q(B1_OUT));  // open: Qn, preset, reset
  D_Flip_Flop d_ff_4 (.D(B0_IN), .clk(MyClock), .Q(B0_OUT));  // open: Qn, preset, reset
endmodule

module Project_Data_RAM (
  input  CLK,
  input  Address_1Bit,
  input  [3:0] Data_Input,
  input  MODE,
  output [3:0] Data_Output
);

  wire and_1_out, and_2_out, B0_I0, B0_I1, B1_I0, B1_I1, B2_I0, B2_I1, B3_I0, B3_I1, decoder_1_out0,
       decoder_1_out1, multiplexer_1_out, multiplexer_2_out, multiplexer_3_out, multiplexer_4_out, not_1_out;

  Decoder #(.enable("false")) decoder_1 (.out0(decoder_1_out0), .out1(decoder_1_out1), .sel(Address_1Bit));
  and and_1 (and_1_out, decoder_1_out0, not_1_out, CLK);
  and and_2 (and_2_out, decoder_1_out1, not_1_out, CLK);
  not not_1 (not_1_out, MODE);
  Multiplexer multiplexer_1 (.in0(B3_I0), .in1(B3_I1), .out(multiplexer_1_out), .sel(Address_1Bit));
  Multiplexer multiplexer_2 (.in0(B2_I0), .in1(B2_I1), .out(multiplexer_2_out), .sel(Address_1Bit));
  Project_MyReg Address_0 (
    .B3_IN(Data_Input[3]), .B2_IN(Data_Input[2]), .B1_IN(Data_Input[1]), .B0_IN(Data_Input[0]),
    .MyClock(and_1_out), .B3_OUT(B3_I0), .B2_OUT(B2_I0), .B1_OUT(B1_I0), .B0_OUT(B0_I0));
  Multiplexer multiplexer_3 (.in0(B1_I0), .in1(B1_I1), .out(multiplexer_3_out), .sel(Address_1Bit));
  Multiplexer multiplexer_4 (.in0(B0_I0), .in1(B0_I1), .out(multiplexer_4_out), .sel(Address_1Bit));
  Project_MyReg Address_1 (
    .B3_IN(Data_Input[3]), .B2_IN(Data_Input[2]), .B1_IN(Data_Input[1]), .B0_IN(Data_Input[0]),
    .MyClock(and_2_out), .B3_OUT(B3_I1), .B2_OUT(B2_I1), .B1_OUT(B1_I1), .B0_OUT(B0_I1));
  and and_3 (Data_Output[1], multiplexer_3_out, MODE);
  and and_4 (Data_Output[0], multiplexer_4_out, MODE);
  and and_5 (Data_Output[3], multiplexer_1_out, MODE);
  and and_6 (Data_Output[2], multiplexer_2_out, MODE);

  // Other names for the same wires on the sheet: B0 = Data_Input[0]; B1 = Data_Input[1]; B2 = Data_Input[2];
  //   B3 = Data_Input[3]; S0 = Address_1Bit

  // Notes on the sheet:
  //   BIT3
  //   BIT2
  //   BIT1
  //   Bit0
endmodule

module ALU2 (
  input  [3:0] A,
  input  [3:0] B,
  input  CLK,
  input  ADD_OR_SUB,
  output [3:0] ALU_Output,
  output [2:0] Status
);

  wire not_2_out, not_3_out, not_4_out, not_5_out;
  wire [3:0] and_1_out, and_2_out, and_3_out, and_7_out, bit_extender_1_out, not_1_out, or_1_out;

  assign bit_extender_1_out = {{3{CLK}}, CLK};  // Bit_Extender bit_extender_1
  assign and_1_out = A & bit_extender_1_out;  // AND_Gate and_1, 4 bits wide
  assign and_2_out = B & bit_extender_1_out;  // AND_Gate and_2, 4 bits wide
  assign not_1_out = ~and_2_out;  // NOT_Gate not_1, 4 bits wide
  not not_2 (not_2_out, ADD_OR_SUB);
  and and_3 (and_3_out[0], not_2_out, and_2_out[0]);
  not not_3 (not_3_out, ADD_OR_SUB);
  and and_4 (and_3_out[1], not_3_out, and_2_out[1]);
  not not_4 (not_4_out, ADD_OR_SUB);
  and and_5 (and_3_out[2], not_4_out, and_2_out[2]);
  not not_5 (not_5_out, ADD_OR_SUB);
  and and_6 (and_3_out[3], not_5_out, and_2_out[3]);
  and and_7 (and_7_out[0], ADD_OR_SUB, not_1_out[0]);
  and and_8 (and_7_out[1], ADD_OR_SUB, not_1_out[1]);
  and and_9 (and_7_out[2], ADD_OR_SUB, not_1_out[2]);
  and and_10 (and_7_out[3], ADD_OR_SUB, not_1_out[3]);
  assign or_1_out = and_3_out | and_7_out;  // OR_Gate or_1, 4 bits wide
  Adder4Bit adder4bit_1 (
    .A(and_1_out), .B(or_1_out), .C_IN(ADD_OR_SUB), .SUM(ALU_Output), .V(Status[2]), .Z(Status[1]));

  assign Status[0] = ALU_Output[3];

  // Notes on the sheet:
  //   ADD => 0
  //   SUB => 1
endmodule

module Project_RegFile (
  input  [3:0] RegIn,
  input  Reg_Select,
  input  CLK,
  output [3:0] R0_Out,
  output [3:0] R1_Out
);

  wire decoder_1_out0, decoder_1_out1;

  Decoder decoder_1 (.out0(decoder_1_out0), .out1(decoder_1_out1), .sel(Reg_Select));  // open: en
  Register #(.width(4)) R0 (.D(RegIn), .en(decoder_1_out0), .clk(CLK), .Q(R0_Out));  // open: clr
  Register #(.width(4)) R1 (.D(RegIn), .en(decoder_1_out1), .clk(CLK), .Q(R1_Out));  // open: clr
endmodule
