// Logisim project project_miniCPU.circ as structural Verilog
module Adder4Bit (
  input  [3:0] A,
  input  [3:0] B,
  input  C_IN,
  output [3:0] SUM,
  output V,
  output Z
);

  wire and_1_out, and_2_out, and_3_out, and_4_out, and_5_out, and_6_out, and_7_out, and_8_out, or_1_out,
       or_2_out, or_3_out, or_4_out, xor_1_out, xor_3_out, xor_5_out, xor_8_out;

  xor xor_1 (xor_1_out, A[0], B[0]);
  xor xor_2 (SUM[0], xor_1_out, C_IN);
  and and_1 (and_1_out, A[0], B[0]);
  or or_1 (or_1_out, and_1_out, and_2_out);
  and and_2 (and_2_out, xor_1_out, C_IN);
  xor xor_3 (xor_3_out, A[1], B[1]);
  xor xor_4 (SUM[1], xor_3_out, or_1_out);
  and and_3 (and_3_out, A[1], B[1]);
  and and_4 (and_4_out, xor_3_out, or_1_out);
  or or_2 (or_2_out, and_3_out, and_4_out);
  nor nor_1 (Z, SUM[3], SUM[2], SUM[1], SUM[0]);
  xor xor_5 (xor_5_out, A[2], B[2]);
  xor xor_6 (SUM[2], xor_5_out, or_2_out);
  and and_5 (and_5_out, A[2], B[2]);
  or or_3 (or_3_out, and_5_out, and_6_out);
  and and_6 (and_6_out, xor_5_out, or_2_out);
  xor xor_7 (V, or_3_out, or_4_out);
  xor xor_8 (xor_8_out, A[3], B[3]);
  xor xor_9 (SUM[3], xor_8_out, or_3_out);
  and and_7 (and_7_out, A[3], B[3]);
  and and_8 (and_8_out, xor_8_out, or_3_out);
  or or_4 (or_4_out, and_7_out, and_8_out);
endmodule

module Mux3to1 (
  input  [3:0] AddSubRESULT,
  input  [1:0] Operation,
  input  [3:0] ANDResult,
  input  [3:0] ORResult,
  output [3:0] Chosen
);

  wire [3:0] and_1_out, and_2_out, and_3_out, and_4_out, and_5_out, and_6_out, bit_extender_1_out,
       bit_extender_2_out, not_1_out, not_2_out;

  assign bit_extender_1_out = {{3{Operation[0]}}, Operation[0]};  // Bit_Extender bit_extender_1
  assign bit_extender_2_out = {{3{Operation[1]}}, Operation[1]};  // Bit_Extender bit_extender_2
  assign not_1_out = ~bit_extender_1_out;  // NOT_Gate not_1, 4 bits wide
  assign not_2_out = ~bit_extender_2_out;  // NOT_Gate not_2, 4 bits wide
  assign and_1_out = not_1_out & not_2_out;  // AND_Gate and_1, 4 bits wide
  assign and_2_out = bit_extender_1_out & not_2_out;  // AND_Gate and_2, 4 bits wide
  assign and_3_out = not_1_out & bit_extender_2_out;  // AND_Gate and_3, 4 bits wide
  assign and_4_out = AddSubRESULT & and_1_out;  // AND_Gate and_4, 4 bits wide
  assign and_5_out = ANDResult & and_2_out;  // AND_Gate and_5, 4 bits wide
  assign and_6_out = ORResult & and_3_out;  // AND_Gate and_6, 4 bits wide
  assign Chosen = and_4_out | and_5_out | and_6_out;  // OR_Gate or_1, 4 bits wide
endmodule

module myReg4Bit (
  input  [3:0] RegIn,
  input  myClock,
  output [3:0] RegOut
);

  D_Flip_Flop d_ff_1 (.D(RegIn[0]), .clk(myClock), .Q(RegOut[0]));  // open: Qn, preset, reset
  D_Flip_Flop d_ff_2 (.D(RegIn[1]), .clk(myClock), .Q(RegOut[1]));  // open: Qn, preset, reset
  D_Flip_Flop d_ff_3 (.D(RegIn[2]), .clk(myClock), .Q(RegOut[2]));  // open: Qn, preset, reset
  D_Flip_Flop d_ff_4 (.D(RegIn[3]), .clk(myClock), .Q(RegOut[3]));  // open: Qn, preset, reset
endmodule

module MyReg3Bit (
  input  [2:0] RegIn,
  input  MyClock,
  output [2:0] RegOut
);

  D_Flip_Flop d_ff_1 (.D(RegIn[0]), .clk(MyClock), .Q(RegOut[0]));  // open: Qn, preset, reset
  D_Flip_Flop d_ff_2 (.D(RegIn[1]), .clk(MyClock), .Q(RegOut[1]));  // open: Qn, preset, reset
  D_Flip_Flop d_ff_3 (.D(RegIn[2]), .clk(MyClock), .Q(RegOut[2]));  // open: Qn, preset, reset
endmodule

module Project_ALU (
  input  [3:0] A,
  input  [3:0] B,
  input  ADD_OR_SUB,
  input  CLK,
  output [3:0] ALU_Output,
  output [2:0] Status
);

  wire not_2_out, not_3_out, not_4_out, not_5_out;
  wire [2:1] adder4bit_1_z;
  wire [3:0] adder4bit_1_sum, and_1_out, and_5_out, myreg4bit_1_regout, myreg4bit_2_regout, not_1_out,
       or_1_out;

  myReg4Bit myreg4bit_1 (.RegIn(A), .myClock(CLK), .RegOut(myreg4bit_1_regout));
  myReg4Bit myreg4bit_2 (.RegIn(B), .myClock(CLK), .RegOut(myreg4bit_2_regout));
  assign not_1_out = ~myreg4bit_2_regout;  // NOT_Gate not_1, 4 bits wide
  not not_2 (not_2_out, ADD_OR_SUB);
  and and_1 (and_1_out[0], not_2_out, myreg4bit_2_regout[0]);
  not not_3 (not_3_out, ADD_OR_SUB);
  and and_2 (and_1_out[1], not_3_out, myreg4bit_2_regout[1]);
  not not_4 (not_4_out, ADD_OR_SUB);
  and and_3 (and_1_out[2], not_4_out, myreg4bit_2_regout[2]);
  not not_5 (not_5_out, ADD_OR_SUB);
  and and_4 (and_1_out[3], not_5_out, myreg4bit_2_regout[3]);
  and and_5 (and_5_out[0], ADD_OR_SUB, not_1_out[0]);
  and and_6 (and_5_out[1], ADD_OR_SUB, not_1_out[1]);
  and and_7 (and_5_out[2], ADD_OR_SUB, not_1_out[2]);
  and and_8 (and_5_out[3], ADD_OR_SUB, not_1_out[3]);
  assign or_1_out = and_1_out | and_5_out;  // OR_Gate or_1, 4 bits wide
  Adder4Bit adder4bit_1 (
    .A(myreg4bit_1_regout), .B(or_1_out), .C_IN(ADD_OR_SUB), .SUM(adder4bit_1_sum), .V(adder4bit_1_z[2]),
    .Z(adder4bit_1_z[1]));
  myReg4Bit myreg4bit_3 (.RegIn(adder4bit_1_sum), .myClock(CLK), .RegOut(ALU_Output));
  MyReg3Bit myreg3bit_1 (.RegIn({adder4bit_1_z, ALU_Output[3]}), .MyClock(CLK), .RegOut(Status));

  // Notes on the sheet:
  //   ADD => 0
  //   SUB => 1
endmodule

module Project_PC (
  input  The_Clock,
  input  Initialize,
  output [2:0] Instruction
);

  wire [3:0] multiplexer_1_out, pc_adder_1_pc_plus_one, register_1_q;
  wire [3:3] register_2_q;

  Multiplexer #(.width(4)) multiplexer_1 (.in0(register_1_q), .in1(4'b0000), .out(multiplexer_1_out), .sel(Initialize));
  Register #(.width(4)) register_1 (.D(pc_adder_1_pc_plus_one), .clk(The_Clock), .Q(register_1_q));  // open: en, clr
  Register #(.width(4)) register_2 (
    .D(multiplexer_1_out), .clk(The_Clock), .Q({register_2_q[3], Instruction}));  // open: en, clr
  PC_Adder pc_adder_1 (.Increment_PC({register_2_q[3], Instruction}), .PC_Plus_One(pc_adder_1_pc_plus_one));
endmodule

module PC_Adder (
  input  [3:0] Increment_PC,
  output [3:0] PC_Plus_One
);

  wire singlebitadder_1_c_out, singlebitadder_2_c_out, singlebitadder_3_c_out;

  SingleBitAdder singlebitadder_1 (
    .A(Increment_PC[0]), .B(1'b0), .C_IN(1'b1), .C_OUT(singlebitadder_1_c_out), .SUM(PC_Plus_One[0]));
  SingleBitAdder singlebitadder_2 (
    .A(Increment_PC[1]), .B(1'b0), .C_IN(singlebitadder_1_c_out), .C_OUT(singlebitadder_2_c_out),
    .SUM(PC_Plus_One[1]));
  SingleBitAdder singlebitadder_3 (
    .A(Increment_PC[2]), .B(1'b0), .C_IN(singlebitadder_2_c_out), .C_OUT(singlebitadder_3_c_out),
    .SUM(PC_Plus_One[2]));
  SingleBitAdder singlebitadder_4 (
    .A(Increment_PC[3]), .B(1'b0), .C_IN(singlebitadder_3_c_out), .SUM(PC_Plus_One[3]));  // open: C_OUT
endmodule

module SingleBitAdder (
  input  A,
  input  B,
  input  C_IN,
  output C_OUT,
  output SUM
);

  wire and_1_out, and_2_out, xor_1_out;

  xor xor_1 (xor_1_out, A, B);
  and and_1 (and_1_out, A, B);
  and and_2 (and_2_out, xor_1_out, C_IN);
  or or_1 (C_OUT, and_1_out, and_2_out);
  xor xor_2 (SUM, xor_1_out, C_IN);
endmodule

module IR (
  input  [3:0] IR_Input,
  input  CLK,
  output [3:0] IR_Output,
  output [3:0] IR_Contents
);

  Register #(.width(4)) register_1 (.D(IR_Input), .clk(CLK), .Q(IR_Contents));  // open: en, clr

  assign IR_Output = IR_Contents;
endmodule

module Data_RAM (
  input  CLK,
  input  Address_1Bit,
  input  [3:0] Data_Input,
  input  MODE,
  output [3:0] Data_Output
);

  wire and_1_out, and_2_out, and_3_out, and_4_out, and_5_out, and_6_out, B0, B0_I0, B0_I1, B1, B1_I0, B1_I1,
       B2, B2_I0, B2_I1, B3, B3_I0, B3_I1, d_ff_1_q, decoder_1_out0, decoder_1_out1, multiplexer_1_out,
       multiplexer_2_out, multiplexer_3_out, multiplexer_4_out, not_1_out, S0;

  // MyReg myreg_1: pin names not known; wires that end beside it: B3, Data_Input[3], B2, Data_Input[2], B1, Data_Input[1], B0, Data_Input[0], CLK
  D_Flip_Flop d_ff_1 (.D(MODE), .clk(CLK), .Q(d_ff_1_q));  // open: Qn, preset, reset
  D_Flip_Flop d_ff_2 (.D(Address_1Bit), .clk(CLK), .Q(S0));  // open: Qn, preset, reset
  Decoder decoder_1 (.out0(decoder_1_out0), .out1(decoder_1_out1), .sel(S0));  // open: en
  and and_1 (and_1_out, decoder_1_out0, not_1_out, CLK);
  and and_2 (and_2_out, decoder_1_out1, not_1_out, CLK);
  not not_1 (not_1_out, d_ff_1_q);
  Multiplexer multiplexer_1 (.in0(B3_I0), .in1(B3_I1), .out(multiplexer_1_out), .sel(S0));
  Multiplexer multiplexer_2 (.in0(B2_I0), .in1(B2_I1), .out(multiplexer_2_out), .sel(S0));
  // MyReg Address_0: pin names not known; wires that end beside it: B3_I0, B3, B2_I0, B2, B1_I0, B1, B0_I0, B0, and_1_out
  Multiplexer multiplexer_3 (.in0(B1_I0), .in1(B1_I1), .out(multiplexer_3_out), .sel(S0));
  Multiplexer multiplexer_4 (.in0(B0_I0), .in1(B0_I1), .out(multiplexer_4_out), .sel(S0));
  // MyReg Address_1: pin names not known; wires that end beside it: B3_I1, B3, B2_I1, B2, B1_I1, B1, B0_I1, B0, and_2_out
  and and_3 (and_3_out, multiplexer_3_out, d_ff_1_q);
  and and_4 (and_4_out, multiplexer_4_out, d_ff_1_q);
  and and_5 (and_5_out, multiplexer_1_out, d_ff_1_q);
  and and_6 (and_6_out, multiplexer_2_out, d_ff_1_q);
  // MyReg myreg_2: pin names not known; wires that end beside it: and_5_out, and_6_out, and_3_out, and_4_out, CLK, Data_Output[0], Data_Output[1], Data_Output[2], Data_Output[3]

  // Notes on the sheet:
  //   BIT3
  //   BIT2
  //   BIT1
  //   Bit0
endmodule

module Instruction_RAM (
  input  CLK,
  input  MODE,
  input  [2:0] Address,
  input  [3:0] Instruction_Input,
  output [3:0] Instruction_Output
);

  wire and_1_out, and_2_out, and_3_out, and_4_out, and_5_out, and_6_out, and_7_out, and_8_out, and_9_out,
       and_10_out, and_11_out, and_12_out, B0, B0_I0, B0_I1, B0_I2, B0_I3, B0_I4, B0_I5, B0_I6, B0_I7, B1,
       B1_I0, B1_I1, B1_I2, B1_I3, B1_I4, B1_I5, B1_I6, B1_I7, B2, B2_I0, B2_I1, B2_I2, B2_I3, B2_I4, B2_I5,
       B2_I6, B2_I7, B3, B3_I0, B3_I1, B3_I2, B3_I3, B3_I4, B3_I5, B3_I6, B3_I7, d_ff_4_q, decoder_1_out0,
       decoder_1_out1, decoder_1_out2, decoder_1_out3, decoder_1_out4, decoder_1_out5, decoder_1_out6,
       decoder_1_out7, multiplexer_1_out, multiplexer_2_out, multiplexer_3_out, multiplexer_4_out, not_1_out;
  wire [2:0] MUX_SELECT;

  D_Flip_Flop d_ff_1 (.D(Address[2]), .clk(CLK), .Q(MUX_SELECT[2]));  // open: Qn, preset, reset
  D_Flip_Flop d_ff_2 (.D(Address[1]), .clk(CLK), .Q(MUX_SELECT[1]));  // open: Qn, preset, reset
  Decoder #(.select(3)) decoder_1 (
    .out0(decoder_1_out0), .out1(decoder_1_out1), .out2(decoder_1_out2), .out3(decoder_1_out3),
    .out4(decoder_1_out4), .out5(decoder_1_out5), .out6(decoder_1_out6), .out7(decoder_1_out7),
    .sel(MUX_SELECT));  // open: en
  D_Flip_Flop d_ff_3 (.D(Address[0]), .clk(CLK), .Q(MUX_SELECT[0]));  // open: Qn, preset, reset
  Multiplexer #(.select(3)) multiplexer_1 (
    .in0(B3_I0), .in1(B3_I1), .in2(B3_I2), .in3(B3_I3), .in4(B3_I4), .in5(B3_I5), .in6(B3_I6), .in7(B3_I7),
    .out(multiplexer_1_out), .sel(MUX_SELECT));
  Multiplexer #(.select(3)) multiplexer_2 (
    .in0(B2_I0), .in1(B2_I1), .in2(B2_I2), .in3(B2_I3), .in4(B2_I4), .in5(B2_I5), .in6(B2_I6), .in7(B2_I7),
    .out(multiplexer_2_out), .sel(MUX_SELECT));
  and and_1 (and_1_out, decoder_1_out0, not_1_out, CLK);
  and and_2 (and_2_out, decoder_1_out1, not_1_out, CLK);
  not not_1 (not_1_out, d_ff_4_q);
  D_Flip_Flop d_ff_4 (.D(MODE), .clk(CLK), .Q(d_ff_4_q));  // open: Qn, preset, reset
  and and_3 (and_3_out, decoder_1_out2, not_1_out, CLK);
  and and_4 (and_4_out, decoder_1_out3, not_1_out, CLK);
  Multiplexer #(.select(3)) multiplexer_3 (
    .in0(B1_I0), .in1(B1_I1), .in2(B1_I2), .in3(B1_I3), .in4(B1_I4), .in5(B1_I5), .in6(B1_I6), .in7(B1_I7),
    .out(multiplexer_3_out), .sel(MUX_SELECT));
  Multiplexer #(.select(3)) multiplexer_4 (
    .in0(B0_I0), .in1(B0_I1), .in2(B0_I2), .in3(B0_I3), .in4(B0_I4), .in5(B0_I5), .in6(B0_I6), .in7(B0_I7),
    .out(multiplexer_4_out), .sel(MUX_SELECT));
  // MyReg REG_0: pin names not known; wires that end beside it: B3_I0, B3, B2_I0, B2, B1_I0, B1, B0_I0, B0, and_1_out
  // MyReg REG_2: pin names not known; wires that end beside it: B3_I2, B3, B2_I2, B2, B1_I2, B1, B0_I2, B0, and_3_out
  // MyReg REG_1: pin names not known; wires that end beside it: B3_I1, B3, B2_I1, B2, B1_I1, B1, B0_I1, B0, and_2_out
  // MyReg REG_3: pin names not known; wires that end beside it: B3_I3, B3, B2_I3, B2, B1_I3, B1, B0_I3, B0, and_4_out
  // MyReg myreg_1: pin names not known; wires that end beside it: B3, Instruction_Input[3], B2, Instruction_Input[2], B1, Instruction_Input[1], B0, Instruction_Input[0], CLK
  and and_5 (and_5_out, multiplexer_3_out, d_ff_4_q);
  and and_6 (and_6_out, multiplexer_4_out, d_ff_4_q);
  and and_7 (and_7_out, multiplexer_1_out, d_ff_4_q);
  and and_8 (and_8_out, multiplexer_2_out, d_ff_4_q);
  and and_9 (and_9_out, decoder_1_out4, not_1_out, CLK);
  and and_10 (and_10_out, decoder_1_out5, not_1_out, CLK);
  // MyReg myreg_2: pin names not known; wires that end beside it: and_7_out, and_8_out, and_5_out, and_6_out, CLK, Instruction_Output[3], Instruction_Output[2], Instruction_Output[1], Instruction_Output[0]
  and and_11 (and_11_out, decoder_1_out6, not_1_out, CLK);
  and and_12 (and_12_out, decoder_1_out7, not_1_out, CLK);
  // MyReg REG_4: pin names not known; wires that end beside it: B3_I4, B3, B2_I4, B2, B1_I4, B1, B0_I4, B0, and_9_out
  // MyReg REG_6: pin names not known; wires that end beside it: B3_I6, B3, B2_I6, B2, B1_I6, B1, B0_I6, B0, and_11_out
  // MyReg REG_5: pin names not known; wires that end beside it: B3_I5, B3, B2_I5, B2, B1_I5, B1, B0_I5, B0, and_10_out
  // MyReg REG_7: pin names not known; wires that end beside it: B3_I7, B3, B2_I7, B2, B1_I7, B1, B0_I7, B0, and_12_out

  // Other names for the same wires on the sheet: S0 = MUX_SELECT[0]; S1 = MUX_SELECT[1]; S2 = MUX_SELECT[2]

  // Notes on the sheet:
  //   CHOOSE_B3
  //   CHOOSE_B2
  //   CHOOSE_B1
  //   CHOOSE_B0
endmodule

module project_main (
  input  Sign_Overflow,
  input  Zero,
  input  Sign,
  input  RW,
  input  Initialize,
  input  [3:0] Setting_Of_Instructions,
  input  [2:0] Choice_Of_Instruction_Address,
  input  Instruction_RAM_Write,
  output [2:0] out_9,
  output [3:0] IR_Contents
);

  wire ADD_OR_SUB, and_2_out, CLK, clock_1_out, cu_1_pc_inc, Data_RAM_Address, Data_RAM_Mode, HALT,
       not_1_out, RAM_OR_ALU, Reg_Read, Reg_Select, Reg_Write;
  wire [2:0] multiplexer_1_out;
  wire [3:0] data_ram_1_data_output, instruction_ram_1_instruction_output, ir_1_ir_output, multiplexer_2_out,
       project_alu_1_alu_output, regfile_1_r0_out, regfile_1_r1_out;

  Clock clock_1 (.out(clock_1_out));
  not not_1 (not_1_out, HALT);
  and and_1 (CLK, clock_1_out, not_1_out);
  and and_2 (and_2_out, cu_1_pc_inc, Instruction_RAM_Write);
  Project_PC project_pc_1 (.The_Clock(and_2_out), .Initialize(Initialize), .Instruction(out_9));
  Multiplexer #(.width(3)) multiplexer_1 (
    .in0(Choice_Of_Instruction_Address), .in1(out_9), .out(multiplexer_1_out), .sel(Instruction_RAM_Write));
  Instruction_RAM instruction_ram_1 (
    .CLK(CLK), .MODE(RW), .Address(multiplexer_1_out), .Instruction_Input(Setting_Of_Instructions),
    .Instruction_Output(instruction_ram_1_instruction_output));
  CU cu_1 (
    .CLK(CLK), .IR_Output(ir_1_ir_output), .RAM_OR_ALU(RAM_OR_ALU), .Reg_Write(Reg_Write),
    .Reg_Read(Reg_Read), .Data_RAM_Mode(Data_RAM_Mode), .ADD_OR_SUB(ADD_OR_SUB),
    .Data_RAM_Address(Data_RAM_Address), .Reg_Select(Reg_Select), .HALT(HALT), .PC_Inc(cu_1_pc_inc));
  IR ir_1 (
    .IR_Input(instruction_ram_1_instruction_output), .CLK(CLK), .IR_Output(ir_1_ir_output),
    .IR_Contents(IR_Contents));
  RegFile regfile_1 (
    .RegIn(multiplexer_2_out), .WriteEnable(Reg_Write), .Reg_Select(Reg_Select), .CLK(CLK),
    .R0_Out(regfile_1_r0_out), .R1_Out(regfile_1_r1_out));  // open: Read_R0, Read_R1
  Project_ALU project_alu_1 (
    .A(regfile_1_r0_out), .B(regfile_1_r1_out), .ADD_OR_SUB(ADD_OR_SUB), .CLK(CLK),
    .ALU_Output(project_alu_1_alu_output), .Status({Sign_Overflow, Zero, Sign}));
  Data_RAM data_ram_1 (
    .CLK(CLK), .Address_1Bit(Data_RAM_Address), .MODE(Data_RAM_Mode), .Data_Output(data_ram_1_data_output));  // open: Data_Input
  Multiplexer #(.width(4)) multiplexer_2 (
    .in0(project_alu_1_alu_output), .in1(data_ram_1_data_output), .out(multiplexer_2_out), .sel(RAM_OR_ALU));

  // Notes on the sheet:
  //   Jim Páircéir 
  //   261243591
  //   Mode (RW) is 0 for initial instruction setting
  //   i.e. Writing the instruction values
  //   Set to 1 when instructions written
  //   Leave at 0 while loading
  //   1 => Read
  //   0 => Write
endmodule

module RegFile (
  input  [3:0] RegIn,
  input  WriteEnable,
  input  Read_R0,
  input  Reg_Select,
  input  Read_R1,
  input  CLK,
  output [3:0] R0_Out,
  output [3:0] R1_Out
);

  wire decoder_1_out0, decoder_1_out1;
  wire [3:0] R0_q, R1_q;

  Decoder decoder_1 (.out0(decoder_1_out0), .out1(decoder_1_out1), .sel(Reg_Select), .en(WriteEnable));
  Register #(.width(4)) R0 (.D(RegIn), .en(decoder_1_out0), .clk(CLK), .Q(R0_q));  // open: clr
  Register #(.width(4)) R1 (.D(RegIn), .en(decoder_1_out1), .clk(CLK), .Q(R1_q));  // open: clr
  Multiplexer #(.width(4)) multiplexer_1 (.in1(R0_q), .out(R0_Out), .sel(Read_R0));  // open: in0
  Multiplexer #(.width(4)) multiplexer_2 (.in1(R1_q), .out(R1_Out), .sel(Read_R1));  // open: in0
endmodule

module CU (
  input  CLK,
  input  [3:0] IR_Output,
  output RAM_OR_ALU,
  output Reg_Write,
  output Reg_Read,
  output Data_RAM_Mode,
  output ADD_OR_SUB,
  output Data_RAM_Address,
  output Reg_Select,
  output HALT,
  output PC_Inc
);

  wire ADD, LOAD, SAVE, SUB;

  Decoder #(.enable("false"), .select(2)) decoder_1 (
    .out0(LOAD), .out1(SAVE), .out2(ADD), .out3(SUB), .sel(IR_Output[3:2]));
  or or_1 (ADD_OR_SUB, ADD, ~SUB);  // OR_Gate
  or or_2 (Data_RAM_Mode, LOAD, ~SAVE);  // OR_Gate
  or or_3 (Reg_Write, LOAD, SUB, ADD);
  or or_4 (Reg_Read, ADD, SUB, SAVE);

  assign Data_RAM_Address = IR_Output[0];
  assign HALT = IR_Output[0];
  assign Reg_Select = IR_Output[1];
endmodule
